// Digital circuit CPU.dig as structural Verilog
module CPU (
  input  RST,
  input  CLK,
  input  clk_2,
  input  CLK_SEL,
  output [7:0] opcode,
  output [15:0] rom
);

  wire A_LD, A_OE, A_SEL, addressdecoder_1_nram_cs, addressdecoder_1_nrom_cs, alu_1_c_flag, alu_1_n_flag,
       alu_1_v_flag, alu_1_z_flag, ALU_CIN, ALU_S0, ALU_S1, ALU_S2, and_1_out, and_2_out, C, CLK_t, FB,
       FL_SEL, I, L_H_SEL, MEM_RD, MEM_WR, N, nALU_OE, nCLI, nFL_LD, nFL_OE, nIR_LD, nIRDB_OE, nMAR_LD,
       nMAR_OE, nMPC_RST, not_1_out, nPC_LD, nPCH_OE, nPCL_OE, nSEI, nSHR, nSP_INC, nSP_LD, nSP_OE, nSPH_OE,
       nSPL_OE, PC_INC, PC_OE, REG_LD, REG_OE, SHR_IN0, sp_1_p6, sp_1_p7, SP_DIR, V, XY_AOE, XY_DIR, XY_INC,
       Z;
  wire [2:0] micropc_1_microstep, Rsrc;
  wire [7:0] ramsingleportsel_1_d;
  wire [15:0] pc_1_p6, rst_buffer_1_a_bus;
  wire [15:5] ctrlunit_1_c32_47;

  not not_1 (not_1_out, RST);
  ADDRESSDECODER addressdecoder_1 (
    .A_BUS(rst_buffer_1_a_bus), .nRAM_CS(addressdecoder_1_nram_cs), .nROM_CS(addressdecoder_1_nrom_cs));  // open: nFB_CS, nMMIO_CS
  RST_Buffer rst_buffer_1 (.RST(not_1_out), .A_BUS(rst_buffer_1_a_bus));
  and and_1 (and_1_out, CLK, ~CLK_SEL);  // And
  and and_2 (and_2_out, CLK_SEL, clk_2);
  or or_1 (CLK_t, and_1_out, and_2_out);
  // PC pc_1: pin names not known; wires that end beside it: rst_buffer_1_a_bus, PC_INC, nPC_LD, CLK_t, RST, pc_1_p6
  // SP sp_1: pin names not known; wires that end beside it: rst_buffer_1_a_bus, nSP_INC, SP_DIR, nSP_LD, CLK_t, sp_1_p6, sp_1_p7
  MAR mar_1 (
    .D_BUS(ramsingleportsel_1_d), .nMAR_OE(nMAR_OE), .nMARL_LD(nMAR_LD), .nMARH_LD(L_H_SEL), .RST(RST),
    .CLK(CLK_t));  // open: A_BUS
  RAMSinglePortSel #(.AddrBits(16), .Bits(8)) ramsingleportsel_1 (
    .A(rst_buffer_1_a_bus), .CS(~addressdecoder_1_nram_cs), .WE(MEM_WR), .OE(MEM_RD), .D(ramsingleportsel_1_d));
  EEPROM #(.AddrBits(15), .Bits(16)) eeprom_1 (
    .A({1'b0, rst_buffer_1_a_bus[13:0]}), .CS(~addressdecoder_1_nrom_cs), .WE(1'b0), .OE(MEM_RD), .D(rom));
  PC_BUFFER pc_buffer_1 (
    .PC(pc_1_p6), .PC_OE(PC_OE), .nPCH_OE(nPCH_OE), .nPCL_OE(nPCL_OE), .RST(RST), .A_BUS(rst_buffer_1_a_bus),
    .D_BUS(ramsingleportsel_1_d));
  // SP_BUFFER sp_buffer_1: pin names not known; wires that end beside it: sp_1_p6, sp_1_p7, nSP_OE, nSPH_OE, nSPL_OE, rst_buffer_1_a_bus, ramsingleportsel_1_d
  IR ir_1 (
    .ROM_IN(rom), .nIR_LD(nIR_LD), .nIRDB_OE(nIRDB_OE), .CLK(CLK_t), ._15_11(opcode[7:3]),
    ._10_8(opcode[2:0]), ._8(L_H_SEL), ._7_5(Rsrc), ._0_7(ramsingleportsel_1_d));
  microPC micropc_1 (.CLK(CLK_t), .nMPC_RST(nMPC_RST), .microstep(micropc_1_microstep));
  RFILE rfile_1 (
    .DB_IN(ramsingleportsel_1_d), .B_10_8(opcode[2:0]), .B_7_5(Rsrc), .REG_LD_EN(REG_LD), .REG_OE_EN(REG_OE),
    .nXY_INC(XY_INC), .XY_DIR(XY_DIR), .nXY_AOE(XY_AOE), .CLK(CLK_t), .RST(RST),
    .DB_OUT(ramsingleportsel_1_d), .AB_OUT(rst_buffer_1_a_bus), .A_LD(A_LD), .A_OE(A_OE));
  ALU alu_1 (
    .D_IN(ramsingleportsel_1_d), .A_LD(A_LD), .A_OE(A_OE), .A_SEL(A_SEL), .ALU_S0(ALU_S0), .ALU_S1(ALU_S1),
    .ALU_S2(ALU_S2), .nALU_OE(nALU_OE), .ALU_CIN(ALU_CIN), .nSHR(nSHR), .SHR_IN0(SHR_IN0), .CLK(CLK_t),
    .RST(RST), .ALU(ramsingleportsel_1_d), .Z_FLAG(alu_1_z_flag), .C_FLAG(alu_1_c_flag),
    .N_FLAG(alu_1_n_flag), .V_FLAG(alu_1_v_flag));  // open: A_R_OUT
  CTRLUNIT ctrlunit_1 (
    .OPC(opcode), .microstep(micropc_1_microstep), .Z(Z), .C(C), .N(N), .V(V), .I(I),
    .C0_15({XY_DIR, XY_INC, REG_OE, REG_LD, nMAR_OE, nMAR_LD, MEM_WR, MEM_RD, nMPC_RST, nIRDB_OE, nIR_LD, nPCH_OE, nPCL_OE, PC_OE, nPC_LD, PC_INC}),
    .C16_31({nSP_INC, FB, nCLI, nSEI, FL_SEL, nFL_LD, nFL_OE, SHR_IN0, nSHR, ALU_CIN, nALU_OE, ALU_S2, ALU_S1, ALU_S0, A_SEL, XY_AOE}),
    .C32_47({ctrlunit_1_c32_47, nSPH_OE, nSPL_OE, nSP_OE, nSP_LD, SP_DIR}));
  FLAG_REG flag_reg_1 (
    .D_IN(ramsingleportsel_1_d), .Z_FLAG(alu_1_z_flag), .C_FLAG(alu_1_c_flag), .N_FLAG(alu_1_n_flag),
    .V_FLAG(alu_1_v_flag), .nFL_OE(nFL_OE), .nFL_LD(nFL_LD), .FL_SEL(FL_SEL), .nSEI(nSEI), .nCLI(nCLI),
    .FB(FB), .CLK(CLK_t), .D_OUT(ramsingleportsel_1_d), .Z(Z), .C(C), .N(N), .V(V), .I(I));

  // Other names for the same wires on the sheet: Rdst[2:0] = opcode[2:0]

  // Notes on the sheet:
  //   clk_2: Hz: 10
  //   contents of eeprom_1 (hex, n*v repeats v):
  //   8f1,1100,101,1500,4300,ac03,ac00,4200,a00,8c10,ac03,ac00
endmodule
